# Fritzing sketch Laser toggle fritzing (saved by Fritzing 0.9.3b)

parts:
  IC2 = IC, DIP package, 14 pins [chip_label=MCP4922 part_number=MCP4922-E/P-ND]
  C2 = Capacitor [part_number=BC1160CT-ND package=cap-pth-small]
  C1 = Capacitor [part_number=BC1160CT-ND package=cap-pth-small]
  C3 = Capacitor [part_number=BC1160CT-ND package=cap-pth-small]
  C4 = Tantalum Capacitor [capacitance=10µF voltage=20V part_number=478-10753-1-ND package="100 mil [THT, tantalum]"]
  C5 = Tantalum Capacitor [capacitance=10µF part_number=478-10753-1-ND voltage=20V package="100 mil [THT, tantalum]"]
  C6 = Capacitor [part_number=BC1160CT-ND package=cap-pth-small]
  J1 = female pin header, 4 pins [form="♀ (female)" part_number=S7002-ND]
  J3 = female pin header, 3 pins [form="♀ (female)" part_number=S7036-NDc]
  Part1 = Adafruit Proto Shield R3 [part_number="Adafruit #2077"]
  U1 = BNC socket [part_number=A97548-ND package=bnc]
  U2 = BNC socket [part_number=A97548-ND package=bnc]
  J2 = female pin header, 3 pins [form="♀ (female)" part_number=S7036-ND]
  J4 = female pin header, 3 pins [form="♀ (female)" part_number=S7036-ND]
  U3 = BNC socket [part_number=A97548-ND package=bnc]
  U4 = BNC socket [part_number=A97548-ND package=bnc]
  S1 = Round Pushbutton [part_number=1528-2317-ND]
  S2 = Round Pushbutton [part_number=1528-2316-ND]
  LED1 = Super Flux LED blue [color=Blue part_number=1528-2317-ND]
  LED2 = smd LED [color="Red (633nm)" part_number=1528-2316-ND package="0603 [SMD]"]
  LCD1 = LCD screen [part_number=NHD-0420DZW-AB5-ND]
  U5 = POT_SWITCH [part_number=PTR901-2015K-B103-ND package=pot_pth_switch]
  U6 = POT_SWITCH [part_number=PTR901-2015K-B103-ND package=pot_pth_switch]
  C7 = Film/Foil Capacitor [capacitance=100nF voltage=35V part_number=445-173377-1-ND package="5mm [THT, pp]"]
  C8 = Film/Foil Capacitor [capacitance=100nF voltage=35V part_number=445-173377-1-ND package="5mm [THT, pp]"]

nets:
  +5V: IC2.pin1, IC2.pin11, IC2.pin13, C2.1, C1.2, C3.1, C4.+, C5.+, C6.1, Part1.+5V, Part1.N$72, Part1.N$81, Part1.N$91, Part1.N$100, Part1.N$193, J4.pin1, J4.pin2, J4.pin3, LCD1.VDD, U5.G$2_2, U6.G$2_2
  N1: IC2.pin2, Part1.N$172
  N2: IC2.pin3, Part1.D8, Part1.N$28
  N3: IC2.pin4, Part1.D13, Part1.N$29, LCD1.DB5
  N4: IC2.pin5, Part1.D11, Part1.N$35, LCD1.DB7
  N5: IC2.pin6, Part1.N$208
  N6: IC2.pin7, Part1.N$209
  N7: IC2.pin8, Part1.D3, Part1.N$75
  N8: IC2.pin9, Part1.N$74
  N9: IC2.pin10, J1.pin1, Part1.N$157, Part1.N$73, U1.OUT
  GND: IC2.pin12, C2.2, C1.1, C3.2, C4.-, C5.-, C6.2, J1.pin2, J1.pin3, J3.pin1, J3.pin2, J3.pin3, Part1.GND, Part1.N$3, Part1.N$6, Part1.N$71, Part1.N$90, U1.GND, U2.GND, J2.pin1, J2.pin2, J2.pin3, U3.GND, U4.GND, S1.leg1, S2.leg0, LED1.cathode, LED2.cathode, LCD1.VSS, U5.G$1_A, U6.G$1_A, C7.+, C8.+
  N10: IC2.pin14, J1.pin4, Part1.N$7, Part1.N$82, U2.OUT
  N11: Part1.D2, U4.OUT
  N12: Part1.D4, S2.leg1
  N13: Part1.D5, LED2.anode
  N14: Part1.D6, LED1.anode
  N15: Part1.D7, S1.leg0
  N16: Part1.A1, U5.G$1_S, C7.-
  N17: Part1.A2, U6.G$1_S, C8.-
  N18: Part1.A0, U3.OUT
  N19: Part1.D9, LCD1.LED+
  N20: Part1.D12, LCD1.DB6
  N21: U5.G$2_1, U5.G$1_E
  N22: U6.G$2_1, U6.G$1_E

custom parts:
  Adafruit Proto Shield R3: This prototyping shield is the best out there (well, we think so, at least), and now is even better with Version R3 - updated for the most compatibility with just about all the Arduinos! It works with UNO, Mega, Leonardo, NG, Diecimila, Duemilanove, and compatible Arduinos. Yun's and Arduino Ethernets have a chunky Ethernet jack that gets in the way of stacking, you can use the stacking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
  POT_SWITCH: Potentiometer w/ switch.
